// Logisim project tmi.circ as structural Verilog: 2 circuits, main circuit main
module main (
);

  wire _0_out, button_2_out, button_out, cell_1_clk_2, cell_1_is_active_2, cell_1_set_head, cell_2_clk_2,
       cell_2_is_active, cell_2_is_active_2, cell_2_set_head, cell_2_set_tail, cell_3_clk_2,
       cell_3_is_active, cell_3_is_active_2, cell_3_set_head, cell_3_set_tail, cell_4_is_active,
       cell_4_set_tail, clock_1_out, priority_encoder_1_p5, priority_encoder_1_p6, priority_encoder_1_p7,
       priority_encoder_1_p8, undriven;
  wire [2:0] cell_1_cmd_2, cell_1_dbg_led, cell_2_cmd_2, cell_2_dbg_led, cell_3_cmd_2, cell_3_dbg_led,
       cell_4_dbg_led, CMD;
  wire [3:0] cell_1_dbg_mem, cell_1_dbg_mem_2, cell_2_dbg_mem, cell_2_dbg_mem_2, cell_3_dbg_mem,
       cell_3_dbg_mem_2, cell_4_dbg_mem, cell_4_dbg_mem_2;
  wire [7:0] cell_1_data_in_2, cell_2_data_in_2, cell_2_data_out_2, cell_3_data_in_2, cell_3_data_out_2,
       cell_4_data_out_2;

  Clock clock_1 (.out(clock_1_out));
  DotMatrix #(.matrixcols(3), .matrixrows(1)) dotmatrix_1 (
    .col0(cell_1_dbg_led[0]), .col1(cell_1_dbg_led[1]), .col2(cell_1_dbg_led[2]));
  Hex_Digit_Display hex_digit_display_1 (.value(cell_1_dbg_mem_2));  // open: dp
  \cell  cell_1 (
    .IS_ACTIVE_LEFT(undriven), .CMD(CMD), .CLK(clock_1_out), .IS_TAIL(cell_2_set_tail),
    .SET_HEAD(cell_1_set_head), .IS_ACTIVE_RIGHT(cell_2_is_active), .IS_ACTIVE_2(cell_1_is_active_2),
    .DATA_IN_2(cell_1_data_in_2), .DATA_OUT(cell_2_data_out_2), .CMD_2(cell_1_cmd_2), .CLK_2(cell_1_clk_2),
    .DBG_MEM({cell_1_dbg_mem_2, cell_1_dbg_mem}), .DBG_LED(cell_1_dbg_led));  // open: SET_TAIL, IS_HEAD, IS_ACTIVE, DATA_IN, DATA_OUT_2
  Hex_Digit_Display hex_digit_display_2 (.value(cell_1_dbg_mem));  // open: dp
  \cell  cell_2 (
    .SET_TAIL(cell_2_set_tail), .IS_HEAD(cell_1_set_head), .IS_ACTIVE(cell_2_is_active),
    .IS_ACTIVE_LEFT(cell_1_is_active_2), .DATA_IN(cell_1_data_in_2), .DATA_OUT_2(cell_2_data_out_2),
    .CMD(cell_1_cmd_2), .CLK(cell_1_clk_2), .IS_TAIL(cell_3_set_tail), .SET_HEAD(cell_2_set_head),
    .IS_ACTIVE_RIGHT(cell_3_is_active), .IS_ACTIVE_2(cell_2_is_active_2), .DATA_IN_2(cell_2_data_in_2),
    .DATA_OUT(cell_3_data_out_2), .CMD_2(cell_2_cmd_2), .CLK_2(cell_2_clk_2),
    .DBG_MEM({cell_2_dbg_mem_2, cell_2_dbg_mem}), .DBG_LED(cell_2_dbg_led));
  DotMatrix #(.matrixcols(3), .matrixrows(1)) dotmatrix_2 (
    .col0(cell_2_dbg_led[0]), .col1(cell_2_dbg_led[1]), .col2(cell_2_dbg_led[2]));
  Hex_Digit_Display hex_digit_display_3 (.value(cell_2_dbg_mem_2));  // open: dp
  Hex_Digit_Display hex_digit_display_4 (.value(cell_2_dbg_mem));  // open: dp
  DotMatrix #(.matrixcols(3), .matrixrows(1)) dotmatrix_3 (
    .col0(cell_3_dbg_led[0]), .col1(cell_3_dbg_led[1]), .col2(cell_3_dbg_led[2]));
  Hex_Digit_Display hex_digit_display_5 (.value(cell_3_dbg_mem_2));  // open: dp
  Button _0 (.out(_0_out));
  \cell  cell_3 (
    .SET_TAIL(cell_3_set_tail), .IS_HEAD(cell_2_set_head), .IS_ACTIVE(cell_3_is_active),
    .IS_ACTIVE_LEFT(cell_2_is_active_2), .DATA_IN(cell_2_data_in_2), .DATA_OUT_2(cell_3_data_out_2),
    .CMD(cell_2_cmd_2), .CLK(cell_2_clk_2), .IS_TAIL(cell_4_set_tail), .SET_HEAD(cell_3_set_head),
    .IS_ACTIVE_RIGHT(cell_4_is_active), .IS_ACTIVE_2(cell_3_is_active_2), .DATA_IN_2(cell_3_data_in_2),
    .DATA_OUT(cell_4_data_out_2), .CMD_2(cell_3_cmd_2), .CLK_2(cell_3_clk_2),
    .DBG_MEM({cell_3_dbg_mem_2, cell_3_dbg_mem}), .DBG_LED(cell_3_dbg_led));
  Hex_Digit_Display hex_digit_display_6 (.value(cell_3_dbg_mem));  // open: dp
  Button button (.out(button_out));
  Button button_2 (.out(button_2_out));
  // Priority_Encoder priority_encoder_1: pin names not known; wires that end beside it: _0_out, button_out, button_2_out, CMD, priority_encoder_1_p5, priority_encoder_1_p6, priority_encoder_1_p7, priority_encoder_1_p8
  \cell  cell_4 (
    .SET_TAIL(cell_4_set_tail), .IS_HEAD(cell_3_set_head), .IS_ACTIVE(cell_4_is_active),
    .IS_ACTIVE_LEFT(cell_3_is_active_2), .DATA_IN(cell_3_data_in_2), .DATA_OUT_2(cell_4_data_out_2),
    .CMD(cell_3_cmd_2), .CLK(cell_3_clk_2), .DBG_MEM({cell_4_dbg_mem_2, cell_4_dbg_mem}),
    .DBG_LED(cell_4_dbg_led));  // open: IS_TAIL, SET_HEAD, IS_ACTIVE_RIGHT, IS_ACTIVE_2, DATA_IN_2, DATA_OUT, CMD_2, CLK_2
  DotMatrix #(.matrixcols(3), .matrixrows(1)) dotmatrix_4 (
    .col0(cell_4_dbg_led[0]), .col1(cell_4_dbg_led[1]), .col2(cell_4_dbg_led[2]));
  Hex_Digit_Display hex_digit_display_7 (.value(cell_4_dbg_mem));  // open: dp
  Hex_Digit_Display hex_digit_display_8 (.value(cell_4_dbg_mem_2));  // open: dp
  Button R (.out(priority_encoder_1_p5));
  Button button_3 (.out(priority_encoder_1_p7));
  Button W (.out(priority_encoder_1_p6));
  Button button_4 (.out(priority_encoder_1_p8));
  Hex_Digit_Display hex_digit_display_9 (.value({1'b0, CMD}));  // open: dp
endmodule

// memcell
module \cell  (
  input  IS_TAIL,
  input  IS_HEAD,
  input  IS_ACTIVE_RIGHT,
  input  IS_ACTIVE_LEFT,
  input  [7:0] DATA_IN,
  input  [7:0] DATA_OUT,
  input  [2:0] CMD,
  input  CLK,
  output SET_TAIL,
  output SET_HEAD,
  output IS_ACTIVE,
  output [7:0] DBG_MEM,
  output [2:0] DBG_LED,
  output IS_ACTIVE_2,
  output [7:0] DATA_IN_2,
  output [7:0] DATA_OUT_2,
  output [2:0] CMD_2,
  output CLK_2
);

  wire and_1_out, and_5_out, and_6_out, bitselector_1_out, bitselector_2_out, COUNT, decoder_1_out0, LOAD,
       minus_ACT, not_1_out, not_2_out, not_3_out, not_4_out, not_5_out, plus_1__1, plus_ACT, R_W, RST,
       s_r_ff_1_q, tunnel, WRITE;
  wire [7:0] controlled_buffer_5_out;

  Pull_Resistor #(.pull(1)) pull_resistor_1 (.node(IS_HEAD));
  Pull_Resistor pull_resistor_2 (.node(IS_ACTIVE_LEFT));
  BitSelector #(.width(2)) bitselector_1 (.in({IS_TAIL, IS_HEAD}), .out(bitselector_1_out), .sel(CMD[0]));
  BitSelector #(.width(2)) bitselector_2 (
    .in({IS_ACTIVE_LEFT, IS_ACTIVE_RIGHT}), .out(bitselector_2_out), .sel(CMD[0]));
  and and_1 (and_1_out, plus_1__1, DBG_LED[1]);
  and and_2 (WRITE, R_W, CMD[0], DBG_LED[1]);
  not not_1 (not_1_out, bitselector_1_out);
  not not_2 (not_2_out, DBG_LED[1]);
  assign LOAD = and_1_out ? CMD[0] : 1'bz;  // Controlled_Buffer controlled_buffer_1
  assign COUNT = and_1_out ? 1'b1 : 1'bz;  // Controlled_Buffer controlled_buffer_2
  assign LOAD = WRITE ? 1'b1 : 1'bz;  // Controlled_Buffer controlled_buffer_3
  assign COUNT = WRITE ? 1'b0 : 1'bz;  // Controlled_Buffer controlled_buffer_4
  Pull_Resistor pull_resistor_3 (.node(DATA_IN));
  Pull_Resistor pull_resistor_4 (.node(DATA_OUT));
  Pull_Resistor pull_resistor_5 (.node(CMD));
  Pull_Resistor pull_resistor_6 (.node(CLK));
  and and_3 (minus_ACT, DBG_LED[1], tunnel, not_1_out);
  and and_4 (plus_ACT, not_2_out, tunnel, bitselector_2_out);
  Pull_Resistor #(.pull(1)) pull_resistor_7 (.node(IS_TAIL));
  Pull_Resistor pull_resistor_8 (.node(IS_ACTIVE_RIGHT));
  assign controlled_buffer_5_out = WRITE ? DATA_IN : 8'bz;  // Controlled_Buffer controlled_buffer_5
  Pull_Resistor pull_resistor_9 (.node(LOAD));
  Pull_Resistor pull_resistor_10 (.node(COUNT));
  Decoder #(.select(2), .disabled(0), .enable("false")) decoder_1 (
    .out0(decoder_1_out0), .out1(tunnel), .out2(R_W), .out3(plus_1__1), .sel(CMD[2:1]));
  not not_3 (not_3_out, CLK);
  S_R_Flip_Flop s_r_ff_1 (.S(plus_ACT), .clk(CLK), .R(minus_ACT), .Q(s_r_ff_1_q), .reset(RST));  // open: Qn, preset, en
  Counter counter_1 (
    .load(LOAD), .D(controlled_buffer_5_out), .count(COUNT), .Q(DBG_MEM), .clk(CLK), .clr(RST));  // open: carry
  and and_5 (and_5_out, not_4_out, DBG_LED[1], R_W);
  not not_4 (not_4_out, CMD[0]);
  and and_6 (and_6_out, CMD[0], decoder_1_out0);
  D_Flip_Flop d_ff_1 (.clk(not_3_out), .D(s_r_ff_1_q), .Q(DBG_LED[1]), .reset(RST));  // open: Qn, preset, en
  assign DATA_OUT = and_5_out ? DBG_MEM : 8'bz;  // Controlled_Buffer controlled_buffer_6
  D_Flip_Flop d_ff_2 (.clk(CLK), .D(and_6_out), .Q(RST), .reset(not_5_out));  // open: Qn, preset, en
  not not_5 (not_5_out, and_6_out);

  assign CLK_2 = CLK;
  assign CMD_2 = CMD;
  assign DATA_IN_2 = DATA_IN;
  assign DATA_OUT_2 = DATA_OUT;
  assign {DBG_LED[2], DBG_LED[0]} = {IS_TAIL, IS_HEAD};
  assign IS_ACTIVE = DBG_LED[1];
  assign IS_ACTIVE_2 = DBG_LED[1];
  assign SET_HEAD = 1'b0;
  assign SET_TAIL = 1'b0;

  // Other names for the same wires on the sheet: AR = IS_ACTIVE_RIGHT; AL = IS_ACTIVE_LEFT; HEAD = IS_HEAD;
  //   ACT = DBG_LED[1]; TAIL = IS_TAIL; IN[7:0] = DATA_IN; OUT[7:0] = DATA_OUT
endmodule
